// Digital circuit CPUv0.dig as structural Verilog
module CPUv0 (
  input  EN,
  input  clk,
  output [15:0] out_3,
  output [3:0] out_4,
  output [15:0] out_5
);

  wire CU_accw, CU_adr_en, CU_lit_en, CU_load_en, CU_mem_r, CU_mem_wr, CU_pc_ow, CU_pcclk, CU_srw,
       CU_unld_en, delay_1_out, delay_2_out;
  wire [3:0] alu_1_f_out, SR_q;
  wire [15:0] alu_1_r, driver_1_out, multiplexer_1_out, SYSMEM_d;
  wire [20:0] INS_d;

  CU CU (
    .ADR_EN(CU_adr_en), .LIT_EN(CU_lit_en), .SRW(CU_srw), .ACCW(CU_accw), .LOAD_EN(CU_load_en),
    .UNLD_EN(CU_unld_en), .MEM_WR(CU_mem_wr), .PC_OW(CU_pc_ow), .PCCLK(CU_pcclk), .F_in(SR_q), .OPC(out_4),
    .ADMD(INS_d[20]), .MEM_R(CU_mem_r), .CLK(clk));
  EEPROM #(.AddrBits(16), .Bits(16)) SYSMEM (.A(driver_1_out), .CS(EN), .WE(CU_mem_wr), .OE(CU_mem_r), .D(SYSMEM_d));
  CounterPreset #(.Bits(16), .isProgramCounter("true")) PC (
    .en(EN), .C(CU_pcclk), .dir(1'b0), .in(INS_d[15:0]), .ld(CU_pc_ow), .clr(1'b0), .out(out_3));  // open: ovf
  ROM #(.AddrBits(16), .Bits(21)) INS (.A(out_3), .sel(EN), .D({INS_d[20], out_4, INS_d[15:0]}));
  assign driver_1_out = CU_adr_en ? INS_d[15:0] : 16'bz;  // Driver driver_1
  assign SYSMEM_d = CU_lit_en ? INS_d[15:0] : 16'bz;  // Driver driver_2
  alu alu_1 (.OPC(out_4), .OP(SYSMEM_d), .ACC(out_5), .F_in(SR_q), .R(alu_1_r), .F_out(alu_1_f_out));
  Multiplexer #(.Bits(16)) multiplexer_1 (.sel(CU_load_en), .in_0(alu_1_r), .in_1(SYSMEM_d), .out(multiplexer_1_out));
  Delay #(.delayTime(5)) delay_1 (.in(CU_srw), .out(delay_1_out));
  Delay #(.delayTime(5)) delay_2 (.in(CU_accw), .out(delay_2_out));
  D_FF #(.Bits(4)) SR (.D(alu_1_f_out), .C(delay_1_out), .Q(SR_q));  // open: nQ
  assign SYSMEM_d = CU_unld_en ? out_5 : 16'bz;  // Driver driver_3
  D_FF #(.Bits(16)) ACC (.D(multiplexer_1_out), .C(delay_2_out), .Q(out_5));  // open: nQ

  // Notes on the sheet:
  //   EN: default 1
  //   clk: Hz: 4
  //   CPU cycle
  //   0 Load Instruction
  //   1 Addressing
  //   2 Write
  //   MEM W
  //   MEM R
  //   PC OW
  //   contents of SYSMEM (hex, n*v repeats v):
  //   d,8,8422*0,78,11458*0,78,3914*0,c42a,22055*0,78,12072*0,85e5,4235*0,78
  //   ADDR EN
  //   LITERAL EN
  //   LOAD EN
  //   contents of INS (hex, n*v repeats v):
  //   0,70001,180000,180001,170000,100001,180000,170001,100000,180001,90004
  //   UNLOAD EN
  //   SR WRITE
  //   ACC WRITE
  //   1 1 2 3 5 8 13 21 34
endmodule
