// Digital circuit CU.dig as structural Verilog
module CU (
  input  [3:0] F_in,
  input  [3:0] OPC,
  input  ADMD,
  input  CLK,
  output ADR_EN,
  output LIT_EN,
  output SRW,
  output ACCW,
  output LOAD_EN,
  output UNLD_EN,
  output MEM_WR,
  output PC_OW,
  output PCCLK,
  output MEM_R
);

  wire and_1_out, and_2_out, and_3_out, and_6_out, and_7_out, and_8_out, and_9_out, multiplexer_1_out,
       nand_1_out, nand_2_out, nor_1_out, not_1_out, not_2_out, not_3_out, not_4_out, not_5_out, not_6_out,
       not_7_out, not_8_out, not_9_out, or_1_out, or_3_out;
  wire [1:0] counter_1_out;

  and and_1 (and_1_out, OPC[3], ~OPC[2], ~OPC[0], ~OPC[1]);  // And
  Counter #(.Bits(2)) counter_1 (.en(1'b1), .C(CLK), .clr(and_3_out), .out(counter_1_out));  // open: ovf
  or or_1 (or_1_out, and_1_out, not_1_out);
  not not_1 (not_1_out, OPC[3]);
  or or_2 (PCCLK, and_2_out, PC_OW);
  and and_2 (and_2_out, or_1_out, nor_1_out);
  nor nor_1 (nor_1_out, counter_1_out[0], counter_1_out[1]);
  and and_3 (and_3_out, ~counter_1_out[0], counter_1_out[1]);  // And
  not not_2 (not_2_out, or_1_out);
  Multiplexer #(.Selector_Bits(3)) multiplexer_1 (
    .sel(OPC[2:0]), .in_0(1'b1), .in_1(1'b1), .in_2(F_in[2]), .in_3(not_3_out), .in_4(F_in[0]),
    .in_5(not_4_out), .in_6(F_in[3]), .in_7(not_5_out), .out(multiplexer_1_out));
  and and_4 (PC_OW, not_2_out, multiplexer_1_out);
  not not_3 (not_3_out, F_in[2]);
  not not_4 (not_4_out, F_in[0]);
  and and_5 (MEM_R, and_9_out, or_3_out);
  not not_5 (not_5_out, F_in[3]);
  and and_6 (and_6_out, ~OPC[0], ~OPC[1], ~OPC[2], OPC[3]);  // And
  not not_6 (not_6_out, and_6_out);
  and and_7 (and_7_out, OPC[0], OPC[1], OPC[2], ~OPC[3]);  // And
  and and_8 (and_8_out, ~OPC[0], OPC[1], OPC[2], ~OPC[3]);  // And
  and and_9 (and_9_out, not_6_out, ADMD);
  not not_7 (not_7_out, and_7_out);
  not not_8 (not_8_out, and_8_out);
  nand nand_1 (nand_1_out, OPC[3], not_7_out);
  nand nand_2 (nand_2_out, OPC[3], not_8_out);
  not not_9 (not_9_out, ADMD);
  or or_3 (or_3_out, counter_1_out[0], counter_1_out[1]);
  and and_10 (ADR_EN, or_3_out, ADMD);
  and and_11 (LIT_EN, not_9_out, or_3_out);
  and and_12 (LOAD_EN, or_3_out, and_7_out);
  and and_13 (UNLD_EN, or_3_out, and_6_out);
  and and_14 (MEM_WR, and_6_out, counter_1_out[1]);
  and and_15 (SRW, counter_1_out[1], nand_1_out);
  and and_16 (ACCW, counter_1_out[1], nand_2_out);
endmodule
