// Digital circuit alu.dig as structural Verilog
module alu (
  input  [3:0] OPC,
  input  [15:0] OP,
  input  [15:0] ACC,
  input  [3:0] F_in,
  output [15:0] R,
  output [3:0] F_out
);

  wire add_1_c_o, and_2_out, driver_1_out, sub_1_c_o;
  wire [1:0] lookuptable_1_out;
  wire [15:0] add_1_s, and_1_out, not_1_out, sub_1_s;

  Add #(.Bits(16)) add_1 (.a(OP), .b(ACC), .c_i(driver_1_out), .s(add_1_s), .c_o(add_1_c_o));
  LookUpTable #(.Bits(2)) lookuptable_1 (.in0(OPC[0]), .in1(OPC[1]), .in2(OPC[2]), .out(lookuptable_1_out));
  assign not_1_out = ~ACC;  // Not not_1, 16 bits wide
  assign and_1_out = ACC & OP;  // And and_1, 16 bits wide
  Multiplexer #(.Selector_Bits(2), .Bits(16)) multiplexer_1 (
    .sel(lookuptable_1_out), .in_0(add_1_s), .in_1(sub_1_s), .in_2(and_1_out), .in_3(not_1_out), .out(R));
  Comparator #(.Signed("true"), .Bits(16)) comparator_1 (
    .a(R), .b({16{1'b0}}), .eq(F_out[2]), .lt(F_out[3]));  // open: gt
  Multiplexer multiplexer_2 (.sel(lookuptable_1_out[0]), .in_0(add_1_c_o), .in_1(sub_1_c_o), .out(F_out[1]));
  Sub #(.Bits(16)) sub_1 (.a(ACC), .b(OP), .c_i(driver_1_out), .s(sub_1_s), .c_o(sub_1_c_o));
  and and_2 (and_2_out, OPC[0], F_in[0]);
  assign driver_1_out = and_2_out ? 1'b1 : 1'bz;  // Driver driver_1
  PullDown pulldown_1 (.out(driver_1_out));
  PullDown #(.Bits(4)) pulldown_2 (.out(F_in));

  assign F_out[0] = F_out[1];

  // Notes on the sheet:
  //   contents of lookuptable_1 (hex, n*v repeats v):
  //   0,28,29,1,2,3,0,0,7,1,2,3,4*7,0,1,3,0,1,3
endmodule
